# Fritzing sketch 3Doodler (saved by Fritzing 0.9.2b)
breadboards: 1

parts:
  Q1 = NPN-Transistor [package="TO92 [THT]"]
  Q2 = NPN-Transistor [package="TO92 [THT]"]
  Part1 = Arduino Uno (Rev3)
  R1 = Resistor [tolerance=±5% resistance=10k package=THT]
  R2 = Resistor [tolerance=±5% resistance=10k package=THT]

nets:
  N1: Q1.E, Q2.E, Part1.GND
  N2: Q1.B, R2.Pin_0
  N3: Q2.B, R1.Pin_0
  N4: Part1.D8, R2.Pin_1
  N5: Part1.D7, R1.Pin_1

notes:
  PIN 0 - GND
  PIN 1 - slow
  PIN 2 - fast
  Arduino fast
  Arduino slow
